# Fritzing sketch AircartoModulePédagogique (saved by Fritzing 0.9.8b)
breadboards: 1

parts:
  Composant1 = Arduino Uno (Rev3) - ICSP
  BAT2 = 18650 battery holder [package=battery-18650-kit]
  Mod1 = SDS011 - dust sensor [part_number=1]
  Composant2 = LCD1602-I2C
  J1 = Piezo Speaker

nets:
  N1: Composant1.A4/SDA, Composant2.SDA
  N2: Composant1.A5/SCL, Composant2.SCL
  5V: Composant1.5V, BAT2.+, Mod1.5V, Composant2.VCC
  N3: Composant1.D8, J1.pin2
  N4: Composant1.D10_PWM/SS, Mod1.TXD
  GND: Composant1.GND, BAT2.-, Mod1.GND, Composant2.GND, J1.pin1

notes:
  Sonde particules fines
  Microcontrôleur Arduino
  Ecran LCD
  Buzzer

custom parts:
  18650 battery holder: 18650 Battery Holder
  SDS011 - dust sensor: The SDS 011 Sensor is a quite recent Air Quality Sensor developed by inovafit, a spin-off from the university of Jinan (in Shandong). With its size, it is probably one of the best sensor in terms of accuracy: While other sensors tend to focus on shrinking the sensor size, the SDS 011 has opted for a size tradeoff allowing it to use a larger fan. And the larger the fan, the better the quality.
  LCD1602-I2C: A standard character display, usually with 2x16 characters. Comes in many colors with LCM1602 IIC attached.
